# Fritzing sketch Circuit (saved by Fritzing 0.9.3b)
breadboards: 1

parts:
  U1 = Vibration Motor- ROB-08449 [package=vibe-motor-10mm]
  U3 = RELAY-SOLIDSTATE [package=relay-s108t02]
  Part1 = Arduino Mega ADK (Rev3)
  U5 = Vibration Motor- ROB-08449 [package=vibe-motor-10mm]
  U6 = RELAY-SOLIDSTATE [package=relay-s108t02]
  U7 = Vibration Motor- ROB-08449 [package=vibe-motor-10mm]
  U8 = RELAY-SOLIDSTATE [package=relay-s108t02]
  U9 = Vibration Motor- ROB-08449 [package=vibe-motor-10mm]
  U10 = RELAY-SOLIDSTATE [package=relay-s108t02]
  U11 = Vibration Motor- ROB-08449 [package=vibe-motor-10mm]
  U12 = RELAY-SOLIDSTATE [package=relay-s108t02]
  U13 = Vibration Motor- ROB-08449 [package=vibe-motor-10mm]
  U14 = RELAY-SOLIDSTATE [package=relay-s108t02]
  U15 = Vibration Motor- ROB-08449 [package=vibe-motor-10mm]
  U16 = RELAY-SOLIDSTATE [package=relay-s108t02]
  U17 = Vibration Motor- ROB-08449 [package=vibe-motor-10mm]
  U18 = RELAY-SOLIDSTATE [package=relay-s108t02]
  U19 = Vibration Motor- ROB-08449 [package=vibe-motor-10mm]
  U20 = RELAY-SOLIDSTATE [package=relay-s108t02]
  U21 = Vibration Motor- ROB-08449 [package=vibe-motor-10mm]
  U22 = RELAY-SOLIDSTATE [package=relay-s108t02]
  U23 = Vibration Motor- ROB-08449 [package=vibe-motor-10mm]
  U24 = RELAY-SOLIDSTATE [package=relay-s108t02]
  U25 = Vibration Motor- ROB-08449 [package=vibe-motor-10mm]
  U26 = RELAY-SOLIDSTATE [package=relay-s108t02]
  U27 = Vibration Motor- ROB-08449 [package=vibe-motor-10mm]
  U28 = RELAY-SOLIDSTATE [package=relay-s108t02]
  U29 = Vibration Motor- ROB-08449 [package=vibe-motor-10mm]
  U30 = RELAY-SOLIDSTATE [package=relay-s108t02]
  U31 = Vibration Motor- ROB-08449 [package=vibe-motor-10mm]
  U32 = RELAY-SOLIDSTATE [package=relay-s108t02]
  U33 = Vibration Motor- ROB-08449 [package=vibe-motor-10mm]
  U34 = RELAY-SOLIDSTATE [package=relay-s108t02]
  Part3 = Triple Axis Accelerometer Breakout - ADXL345
  Raspberry_Pi_1 = Raspberry Pi 3 [part_number=RPI-3-V1.2]  # not connected
  Part4 = BME280 Breakout  # not connected
  U36 = RELAY-SOLIDSTATE [package=relay-s108t02]
  S1 = Round Pushbutton
  R1 = Resistor [tolerance=±5% resistance=220 package="1206 [SMD]"]

nets:
  N1: U1.+, U3.-, U5.+, U6.-, U7.+, U8.-, U9.+, U10.-, U11.+, U12.-, U13.+, U14.-, U15.+, U16.-, U17.+, U18.-, U19.+, U20.-, U21.+, U22.-, U23.+, U24.-, U25.+, U26.-, U27.+, U28.-, U29.+, U30.-, U31.+, U32.-, U33.+, U34.-, Part3.GND, U36.-
  N2: U1.-, U3.T1
  N3: U3.T2, U6.T2, U8.T2, U10.T2, U12.T2, U14.T2, U16.T2, U18.T2, U20.T2, U22.T2, U24.T2, U26.T2, U28.T2, U30.T2, U32.T2, U34.T2, Part3.VCC
  N4: U3.+, Part1.D15/RX3
  N5: Part1.A15, U36.+
  N6: Part1.D21/SCL, Part3.SCL
  N7: Part1.D20/SDA, Part3.SDA
  N8: Part1.D14/TX3, U6.+
  N9: Part1.D13_PWM, U34.+
  N10: Part1.D12_PWM, U32.+
  N11: Part1.D11_PWM, U30.+
  N12: Part1.D10_PWM, U28.+
  N13: Part1.D9_PWM, U26.+
  N14: Part1.D8_PWM, U24.+
  N15: Part1.5V, S1.leg1
  N16: Part1.GND, R1.Pin_1
  N17: Part1.D0/RX0, U8.+
  N18: Part1.D1/TX0, U10.+
  N19: Part1.D2_PWM, U12.+
  N20: Part1.D3_PWM, U14.+
  N21: Part1.D4_PWM, U16.+
  N22: Part1.D5_PWM, U18.+
  N23: Part1.D6_PWM, U20.+
  N24: Part1.D7_PWM, U22.+
  N25: Part1.D49, S1.leg0, R1.Pin_0
  N26: U5.-, U6.T1
  N27: U7.-, U8.T1
  N28: U9.-, U10.T1
  N29: U11.-, U12.T1
  N30: U13.-, U14.T1
  N31: U15.-, U16.T1
  N32: U17.-, U18.T1
  N33: U19.-, U20.T1
  N34: U21.-, U22.T1
  N35: U23.-, U24.T1
  N36: U25.-, U26.T1
  N37: U27.-, U28.T1
  N38: U29.-, U30.T1
  N39: U31.-, U32.T1
  N40: U33.-, U34.T1

notes:
  This is the enclosed High Power Relay. The plug goes into the Normally Open terminal.
  Arduino to Rasp Pi via USB, Raspi to Wall Adapter
  All Wall adapters to non-switching power strip, but with surge protection. Power strip to Wall
  Raspberry Pi Screen Uses Wall Plug and HDMI among other included cables
